# Fritzing sketch connections (saved by Fritzing 0.9.9b)
breadboards: 1

parts:
  MCU1 = Raspberry Pi A
  KY-1 = Keyes Relay [package=THT]
  Part4 = Lilypad Battery Connect
  LED1 = LEDs [package=led10mm]

nets:
  N1: MCU1.pin_1, MCU1.pin_17, KY-1.signal
  N2: MCU1.pin_8, KY-1.power
  N3: MCU1.pin_9, MCU1.pin_25, KY-1.ground
  N4: KY-1.NC, LED1.A
  N5: KY-1.C, Part4.+
  N6: Part4.-, LED1.C

custom parts:
  Raspberry Pi A: The awesome Raspberry Pi ARM Board Jan 2018: Changed schematic to match the other pi boards (connector split by side so one set of pins is on one side of the schematic and the other set is on the opposite side of the schematic so it matches breadboard view. In pcb view reduced the hole size from .047in to the standard .038in for .1 header pins. For all views changed the pin numbers to match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
  Keyes Relay: The Keyes 5V relay module is suitable for SCM development, home appliance control. It uses a 5V~12V TIL control signal which can control DC / AC signal.
  LEDs: LEDs Standard schematic elements and footprints for 5mm, 3mm, 1206, and 0603 sized LEDs. 5mm - Spark Fun Electronics SKU : COM-00529 (and others)
